# Fritzing sketch servos_pi (saved by Fritzing 0.9.4)

parts:
  Raspberry_Pi_1 = Raspberry Pi 3 [part_number=RPI-3-V1.2]
  MICRO_SERVO_SG90_9g = Basic Servo

nets:
  3V3: Raspberry_Pi_1.3v3, MICRO_SERVO_SG90_9g.vcc
  N1: Raspberry_Pi_1.GIPO4, MICRO_SERVO_SG90_9g.pulse
  GND: Raspberry_Pi_1.GND, MICRO_SERVO_SG90_9g.gnd
